// Logisim project 2.circ as structural Verilog: 4 circuits, main circuit main
module main (
  input  [4:0] Reg1_num,
  input  [4:0] Reg2,
  input  [4:0] Write_Reg_num,
  input  [31:0] Din,
  input  Write_Enable,
  input  Clock,
  output [31:0] Reg1,
  output [31:0] s0_Value,
  output [31:0] s1_Value,
  output [31:0] s2_Value,
  output [31:0] ra_Value,
  output [31:0] Reg2_2
);


  // Other names for the same wires on the sheet: clk = Clock; ra[31:0] = ra_Value; reg2_num[4:0] = Reg2;
  //   reg2_t[31:0] = Reg2_2; s0[31:0] = s0_Value; s1[31:0] = s1_Value; s2[31:0] = s2_Value; WE = Write_Enable;
  //   write_data[31:0] = Din

  // Notes on the sheet:
  //   输入引脚
  //   输出引脚
  //   Debug引脚，便于观测寄存器值
  //   请勿修改引脚以及封装，直接使用隧道连接电路
endmodule

module test (
);

  wire undriven;

  main main_1 (.Clock(undriven));  // open: Reg1_num, Reg2, Write_Reg_num, Din, Write_Enable, Reg1, Reg2_2, s0_Value, s1_Value, s2_Value, ra_Value
endmodule

module mips (
  input  [4:0] R1_num,
  input  [4:0] R2_num,
  input  [4:0] W_num,
  input  [31:0] Din,
  input  WE,
  input  CLK
);

  Decoder #(.select(2), .enable("false")) decoder_1 ();  // open: out0, out1, out2, out3, sel
  \reg  reg_1 ();  // open: r1Out, r2Out, directOut, raw1, column1, raw2, column2, writeRaw, writeColumn, WE, CLK, reset, inData
  \reg  reg_2 ();  // open: r1Out, r2Out, directOut, raw1, column1, raw2, column2, writeRaw, writeColumn, WE, CLK, reset, inData
  \reg  reg_3 ();  // open: r1Out, r2Out, directOut, raw1, column1, raw2, column2, writeRaw, writeColumn, WE, CLK, reset, inData
  \reg  reg_4 ();  // open: r1Out, r2Out, directOut, raw1, column1, raw2, column2, writeRaw, writeColumn, WE, CLK, reset, inData
  \reg  reg_5 ();  // open: r1Out, r2Out, directOut, raw1, column1, raw2, column2, writeRaw, writeColumn, WE, CLK, reset, inData
  \reg  reg_6 ();  // open: r1Out, r2Out, directOut, raw1, column1, raw2, column2, writeRaw, writeColumn, WE, CLK, reset, inData
  \reg  reg_7 ();  // open: r1Out, r2Out, directOut, raw1, column1, raw2, column2, writeRaw, writeColumn, WE, CLK, reset, inData
  \reg  reg_8 ();  // open: r1Out, r2Out, directOut, raw1, column1, raw2, column2, writeRaw, writeColumn, WE, CLK, reset, inData
  \reg  reg_9 ();  // open: r1Out, r2Out, directOut, raw1, column1, raw2, column2, writeRaw, writeColumn, WE, CLK, reset, inData
  \reg  reg_10 ();  // open: r1Out, r2Out, directOut, raw1, column1, raw2, column2, writeRaw, writeColumn, WE, CLK, reset, inData
  \reg  reg_11 ();  // open: r1Out, r2Out, directOut, raw1, column1, raw2, column2, writeRaw, writeColumn, WE, CLK, reset, inData
  \reg  reg_12 ();  // open: r1Out, r2Out, directOut, raw1, column1, raw2, column2, writeRaw, writeColumn, WE, CLK, reset, inData
  \reg  reg_13 ();  // open: r1Out, r2Out, directOut, raw1, column1, raw2, column2, writeRaw, writeColumn, WE, CLK, reset, inData
  \reg  reg_14 ();  // open: r1Out, r2Out, directOut, raw1, column1, raw2, column2, writeRaw, writeColumn, WE, CLK, reset, inData
  \reg  reg_15 ();  // open: r1Out, r2Out, directOut, raw1, column1, raw2, column2, writeRaw, writeColumn, WE, CLK, reset, inData
  \reg  reg_16 ();  // open: r1Out, r2Out, directOut, raw1, column1, raw2, column2, writeRaw, writeColumn, WE, CLK, reset, inData
  \reg  reg_17 ();  // open: r1Out, r2Out, directOut, raw1, column1, raw2, column2, writeRaw, writeColumn, WE, CLK, reset, inData
  \reg  reg_18 ();  // open: r1Out, r2Out, directOut, raw1, column1, raw2, column2, writeRaw, writeColumn, WE, CLK, reset, inData
  \reg  reg_19 ();  // open: r1Out, r2Out, directOut, raw1, column1, raw2, column2, writeRaw, writeColumn, WE, CLK, reset, inData
  \reg  reg_20 ();  // open: r1Out, r2Out, directOut, raw1, column1, raw2, column2, writeRaw, writeColumn, WE, CLK, reset, inData
  \reg  reg_21 ();  // open: r1Out, r2Out, directOut, raw1, column1, raw2, column2, writeRaw, writeColumn, WE, CLK, reset, inData
  \reg  reg_22 ();  // open: r1Out, r2Out, directOut, raw1, column1, raw2, column2, writeRaw, writeColumn, WE, CLK, reset, inData
  \reg  reg_23 ();  // open: r1Out, r2Out, directOut, raw1, column1, raw2, column2, writeRaw, writeColumn, WE, CLK, reset, inData
  \reg  reg_24 ();  // open: r1Out, r2Out, directOut, raw1, column1, raw2, column2, writeRaw, writeColumn, WE, CLK, reset, inData
  \reg  reg_25 ();  // open: r1Out, r2Out, directOut, raw1, column1, raw2, column2, writeRaw, writeColumn, WE, CLK, reset, inData
  \reg  reg_26 ();  // open: r1Out, r2Out, directOut, raw1, column1, raw2, column2, writeRaw, writeColumn, WE, CLK, reset, inData
  \reg  reg_27 ();  // open: r1Out, r2Out, directOut, raw1, column1, raw2, column2, writeRaw, writeColumn, WE, CLK, reset, inData
  \reg  reg_28 ();  // open: r1Out, r2Out, directOut, raw1, column1, raw2, column2, writeRaw, writeColumn, WE, CLK, reset, inData
  \reg  reg_29 ();  // open: r1Out, r2Out, directOut, raw1, column1, raw2, column2, writeRaw, writeColumn, WE, CLK, reset, inData
  \reg  reg_30 ();  // open: r1Out, r2Out, directOut, raw1, column1, raw2, column2, writeRaw, writeColumn, WE, CLK, reset, inData
  \reg  reg_31 ();  // open: r1Out, r2Out, directOut, raw1, column1, raw2, column2, writeRaw, writeColumn, WE, CLK, reset, inData
  \reg  reg_32 ();  // open: r1Out, r2Out, directOut, raw1, column1, raw2, column2, writeRaw, writeColumn, WE, CLK, reset, inData
endmodule

module \reg  (
  input  [31:0] inData,
  input  raw1,
  input  column1,
  input  raw2,
  input  column2,
  input  writeRaw,
  input  writeColumn,
  input  WE,
  input  CLK,
  input  reset,
  output [31:0] r1Out,
  output [31:0] r2Out,
  output [31:0] directOut
);

  wire and_1_out, and_2_out, and_3_out, canRead_out;

  assign r1Out = and_1_out ? directOut : 32'bz;  // Controlled_Buffer r1
  and and_1 (and_1_out, raw1, column1, canRead_out);
  assign r2Out = and_2_out ? directOut : 32'bz;  // Controlled_Buffer r2
  and and_2 (and_2_out, raw2, column2, canRead_out);
  nand canRead (canRead_out, CLK, WE);
  and and_3 (and_3_out, writeRaw, writeColumn, WE);
  Register #(.width(32)) register_1 (.D(inData), .en(and_3_out), .Q(directOut), .clk(CLK), .clr(reset));
endmodule
